// Logisim project Exercise2b.circ as structural Verilog: 1 circuit, main circuit main
module main (
  input  A,
  input  B,
  output Greater,
  output out_4,
  output Equal
);

  wire and_3_out, and_4_out, not_1_out, not_2_out;

  not not_1 (not_1_out, A);
  not not_2 (not_2_out, B);
  and and_1 (Greater, A, not_2_out);
  and and_2 (out_4, not_1_out, B);
  and and_3 (and_3_out, A, B);
  or or_1 (Equal, and_3_out, and_4_out);
  and and_4 (and_4_out, not_1_out, not_2_out);

  // Notes on the sheet:
  //              Less than
  //   Nobel Manaye
  //   Exercise 2b
endmodule
