// Logisim project Exercise2c.circ as structural Verilog: 1 circuit, main circuit main
module main (
  input  A_3,
  input  B_3,
  input  A_2,
  input  B_2,
  input  A_1,
  input  B_1,
  input  A_0,
  input  A_0_2,
  output EQUAL
);

  wire and_1_out, and_2_out, and_3_out, and_4_out, and_5_out, and_7_out, and_8_out, and_9_out, and_10_out,
       and_11_out, and_12_out, and_13_out, and_14_out, and_15_out, and_16_out, and_17_out, and_18_out,
       and_19_out, not_1_out, not_2_out, not_3_out, not_4_out, not_5_out, not_6_out, not_7_out, not_8_out,
       not_9_out, or_1_out, or_2_out, or_3_out, or_4_out;

  not not_1 (not_1_out, A_3);
  not not_2 (not_2_out, B_3);
  and and_1 (and_1_out, A_3, not_2_out);
  not not_3 (not_3_out, A_2);
  not not_4 (not_4_out, B_2);
  not not_5 (not_5_out, A_1);
  not not_6 (not_6_out, B_1);
  not not_7 (not_7_out, A_0);
  not not_8 (not_8_out, A_0_2);
  and and_2 (and_2_out, not_1_out, B_3, B_3);
  and and_3 (and_3_out, A_2, not_4_out);
  and and_4 (and_4_out, not_3_out, B_2);
  and and_5 (and_5_out, A_1, not_6_out);
  // AND_Gate and_6 has open pins: in1=not_5_out, in3=B_1, out=open
  and and_7 (and_7_out, A_0, not_8_out);
  and and_8 (and_8_out, not_7_out, A_0_2);
  and and_9 (and_9_out, A_3, B_3);
  or or_1 (or_1_out, and_9_out, and_10_out);
  and and_10 (and_10_out, not_1_out, not_2_out);
  and and_11 (and_11_out, A_2, and_4_out, B_2);
  and and_12 (and_12_out, not_3_out, not_4_out);
  and and_13 (and_13_out, A_1, B_1);
  and and_14 (and_14_out, not_5_out, not_6_out);
  and and_15 (and_15_out, A_0, A_0_2);
  and and_16 (and_16_out, not_7_out, not_8_out);
  or or_2 (or_2_out, and_11_out, and_11_out, and_12_out);
  or or_3 (or_3_out, and_13_out, and_14_out);
  or or_4 (or_4_out, and_15_out, and_16_out);
  and and_17 (and_17_out, and_1_out, and_2_out, and_7_out, and_5_out);
  and and_18 (and_18_out, or_2_out, and_4_out, or_4_out, and_3_out, or_3_out);
  not not_9 (not_9_out, and_19_out);
  and and_19 (and_19_out, and_17_out, and_18_out);
  and and_20 (EQUAL, or_1_out, not_9_out, not_9_out);

  // Notes on the sheet:
  //   Nobel Manaye
  //   Exercise 2 c)
endmodule
