// Logisim project Exercise3.circ as structural Verilog: 1 circuit, main circuit main
module main (
  input  B_inverter,
  input  Carry_in,
  input  A,
  input  B,
  input  in_5,
  input  in_6,
  output Output,
  output out_8
);

  wire adder_1_out, and_1_out, and_2_out, and_3_out, and_4_out, and_5_out, and_6_out, and_7_out, not_1_out,
       not_2_out, not_3_out, not_4_out, or_1_out, or_2_out;

  not not_1 (not_1_out, B);
  and and_1 (and_1_out, B, not_2_out);
  not not_2 (not_2_out, B_inverter);
  and and_2 (and_2_out, not_1_out, B_inverter);
  or or_1 (or_1_out, and_1_out, and_2_out, and_2_out);
  Adder #(.width(1)) adder_1 (.a(A), .b(or_1_out), .out(adder_1_out), .cin(Carry_in), .cout(out_8));
  and and_3 (and_3_out, A, B, B);
  or or_2 (or_2_out, A, B);
  not not_3 (not_3_out, in_5);
  not not_4 (not_4_out, in_6);
  and and_4 (and_4_out, and_3_out, not_3_out, not_4_out);
  and and_5 (and_5_out, or_2_out, not_3_out, in_6);
  and and_6 (and_6_out, adder_1_out, in_5, not_4_out);
  and and_7 (and_7_out, in_5, in_6);
  or or_3 (Output, and_4_out, and_5_out, and_6_out, and_7_out);

  // Notes on the sheet:
  //   Nobel Manaye
  //   Exercise 3
  //   Multiplexor 1
  //   Adder
  //   Or gate
  //   And gate
  //   Carry out
  //   Multipx.Selectors
  //   Multiplexor 2
endmodule
